# Fritzing sketch cpen212_project2 (saved by Fritzing 0.9.4)
breadboards: 1

parts:
  Raspberry_Pi_1 = Raspberry Pi 3 [part_number=RPI-3-V1.2]
  S1 = Pushbutton [package="[SMD]"]
  HC-SR04_Sensor_1 = HC-SR04 Ultrasonic Distance Sensor
  HC-SR04_Sensor_2 = HC-SR04 Ultrasonic Distance Sensor
  HC-SR04_Sensor_3 = HC-SR04 Ultrasonic Distance Sensor
  Part2 = Adafruit 1.44 inch TFT Breakout [part_number="Adafruit #2088"]
  L298N2 = L298N DC motor driver
  M3 = DC Motor
  IC1 = Rasberry Pi NIOR Camera [chip_label=IC package="DIP (Dual Inline) [THT]"]  # not connected
  R1 = Resistor [tolerance=±5% resistance=10k package="0603 [SMD]"]
  M5 = DC Motor
  M6 = DC Motor
  M7 = DC Motor
  BAT1 = Battery Holders [package=battery-aaa]
  BAT2 = Battery Holders [package=battery-aaa]
  BAT3 = Battery Holders [package=battery-aaa]
  BAT4 = Battery Holders [package=battery-aaa]
  SPKR1 = Loudspeaker  # not connected

nets:
  3V3: Raspberry_Pi_1.3v3, Part2.VIN
  N1: Raspberry_Pi_1.GPIO4, S1.Pin_3, S1.Pin_4, R1.Pin_1
  GND: Raspberry_Pi_1.GND, HC-SR04_Sensor_1.GND, HC-SR04_Sensor_2.GND, HC-SR04_Sensor_3.GND, Part2.GND, R1.Pin_0
  N2: Raspberry_Pi_1.GPIO27, HC-SR04_Sensor_1.ECHO
  N3: Raspberry_Pi_1.GPIO10, Part2.MOSI
  N4: Raspberry_Pi_1.GPIO11, Part2.SCK
  N5: Raspberry_Pi_1.GPIO5, L298N2.IN4
  N6: Raspberry_Pi_1.GPIO6, L298N2.IN3
  N7: Raspberry_Pi_1.GPIO13, L298N2.IN2
  N8: Raspberry_Pi_1.GPIO19, L298N2.IN1
  N9: Raspberry_Pi_1.GPIO26, HC-SR04_Sensor_3.TRIG
  N10: Raspberry_Pi_1.GPIO21, HC-SR04_Sensor_2.TRIG
  N11: Raspberry_Pi_1.GPIO20, HC-SR04_Sensor_2.ECHO
  N12: Raspberry_Pi_1.GPIO16, HC-SR04_Sensor_3.ECHO
  N13: Raspberry_Pi_1.GPIO7, HC-SR04_Sensor_1.TRIG
  N14: Raspberry_Pi_1.GPIO8, Part2.TFTCS
  N15: Raspberry_Pi_1.GPIO25, Part2.TFTDC
  N16: Raspberry_Pi_1.GPIO24, Part2.RESET
  VCC: Raspberry_Pi_1.5V, S1.Pin_1, S1.Pin_2, HC-SR04_Sensor_1.VCC, HC-SR04_Sensor_2.VCC, HC-SR04_Sensor_3.VCC
  N17: L298N2.OUT1, M6.pin_2, M7.pin_2
  N18: L298N2.OUT2, M6.pin_1, M7.pin_1
  N19: L298N2.OUT3, M3.pin_2, M5.pin_2
  N20: L298N2.OUT4, M3.pin_1, M5.pin_1
  N21: L298N2.GND, BAT4.-
  N22: L298N2.5V, BAT1.+
  N23: BAT1.-, BAT2.+
  N24: BAT2.-, BAT3.+
  N25: BAT3.-, BAT4.+

notes:
  Pi Camera Module connects to CSI (CAMERA) on Raspberry Pi
  External speaker connects to Audio jack port on Raspberry Pi

custom parts:
  Adafruit 1.44 inch TFT Breakout: This lovely little display breakout is the best way to add a small, colorful and bright display to any project. Since the display uses 4-wire SPI to communicate and has its own pixel-addressable frame buffer, it can be used with every kind of microcontroller. Even a very small one with low memory and few pins available! The 1.44" display has 128x128 color pixels. Unlike the low cost "Nokia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
  L298N DC motor driver: 2x DC motor driver with 78M05 positive voltage regulator (7..35 V) L298N: max 46 V, 2 A Set 5 V Enable jumper to enable 5 V regultor (needed for the L298N) and +5 V output at screw terminal or supply external +5 V at screw terminal Set ENA and/or ENB to +5 V to enable motor permanently or supply ENA and/or ENB with PWM signal IN1 and IN2 set rotation directory for motor A (OUT1/OUT2) IN2 and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
  Rasberry Pi NIOR Camera: Camera
